# Fritzing sketch Sun Shade Electrical Circuit Diagram (saved by Fritzing 0.9.6b)
breadboards: 1

parts:
  A4988_Stepper_Motor_Driver = Pololu A4988 [package=SO16]
  Microcontroller = Arduino Uno (Rev3)
  Left_LDR_Sensor = Photocell (LDR) [package=THT]
  Right_LDR_Sensor = Photocell (LDR) [package=THT]
  Solenoid = Solenoid
  Switch_1 = SWITCH-SPST-2 [package=switch-spst-vertical]
  Switch_2 = SWITCH-SPST-2 [package=switch-spst-vertical]
  R1 = Resistor [tolerance=±5% resistance=10k power=0.25 package=THT]
  R2 = Resistor [tolerance=±5% power=0.25 resistance=10k package=THT]
  DC_Battery = DC Power [voltage=18.5V]
  DC-_DC_Buck_Convertor = IC, DIP package, 4 pins
  Part1 = SO-24x [chip_label=SO-24x package=SO(x)]  # not connected
  Solar_Panel = SIP - 2 pins [package="SIP (Single Inline) [THT]"]
  Solar_Charger = IC, DIP package, 4 pins
  R3 = Resistor [tolerance=±5% power=0.25 resistance=1k package=THT]
  D1 = Rectifier Diode [part_number=1N4001 package="300 mil [THT]"]
  Q1 = npn-Powertransistor [package="TO220 [THT]"]
  Bipolar_Stepper_Motor = IC, SIP package, 4 pins

nets:
  N1: A4988_Stepper_Motor_Driver.ENABLE, Microcontroller.D5_PWM
  N2: A4988_Stepper_Motor_Driver.RESET, A4988_Stepper_Motor_Driver.SLEEP
  N3: A4988_Stepper_Motor_Driver.STEP, Microcontroller.D10_PWM/SS
  N4: A4988_Stepper_Motor_Driver.DIR, Microcontroller.D11_PWM/MOSI
  GND: A4988_Stepper_Motor_Driver.GND, Microcontroller.GND, Solenoid.pin1, R1.Pin_0, R2.Pin_0, DC-_DC_Buck_Convertor.pin2, DC-_DC_Buck_Convertor.pin3, D1.anode
  VDD: A4988_Stepper_Motor_Driver.VDD, Microcontroller.5V, Left_LDR_Sensor.pin_1, Right_LDR_Sensor.pin_1, Q1.collector
  N5: A4988_Stepper_Motor_Driver.1B, Bipolar_Stepper_Motor.pin4
  N6: A4988_Stepper_Motor_Driver.1A, Bipolar_Stepper_Motor.pin2
  N7: A4988_Stepper_Motor_Driver.2A, Bipolar_Stepper_Motor.pin1
  N8: A4988_Stepper_Motor_Driver.2B, Bipolar_Stepper_Motor.pin3
  N9: A4988_Stepper_Motor_Driver.VMOT, Microcontroller.VIN, DC-_DC_Buck_Convertor.pin4
  N10: Microcontroller.A0, Left_LDR_Sensor.pin_0, R2.Pin_1
  N11: Microcontroller.A1, Right_LDR_Sensor.pin_0, R1.Pin_1
  N12: Microcontroller.D2, R3.Pin_0
  N13: Solenoid.pin2, D1.cathode, Q1.emitter
  N14: Switch_1.O, Solar_Charger.pin1
  N15: Switch_1.P, Switch_2.P, DC_Battery.V+
  N16: Switch_2.O, DC-_DC_Buck_Convertor.pin1
  N17: DC_Battery.V-, Solar_Charger.pin2
  N18: Solar_Panel.pin1, Solar_Charger.pin4
  N19: Solar_Panel.pin2, Solar_Charger.pin3
  N20: R3.Pin_1, Q1.base

notes:
  Team-02 Group Project Sose21, TITLE BLOCK, 1.0
  Stepdown: 18.5V to 12V
  12V
  18.5V
  5V
  NPN Transistor
  Diode
  NEMA17
  15W 12-18V
  MPPT Solar Controller(Battery Charger Module)
  GND
  +
  -
